# Fritzing sketch course 5 (saved by Fritzing 1.0.5)
breadboards: 1

parts:
  LED1 = LED - 3mm [color="Red (633nm)" current=0.030A package="3 mm [THT]"]
  LED2 = LED - 3mm [color="Red (633nm)" current=0.030A package="3 mm [THT]"]
  LED3 = LED - 3mm [color="Red (633nm)" current=0.030A package="3 mm [THT]"]
  LED4 = LED - 3mm [color="Red (633nm)" current=0.030A package="3 mm [THT]"]
  R1 = Resistor [tolerance=±5% power=0.25W resistance=220 package=THT]
  R2 = Resistor [tolerance=±5% power=0.25W resistance=220 package=THT]
  R3 = Resistor [tolerance=±5% power=0.25W resistance=220 package=THT]
  R4 = Resistor [tolerance=±5% power=0.25W resistance=220 package=THT]
  Part1 = Arduino Uno (Rev3)

nets:
  N1: LED1.cathode, LED2.cathode, LED3.cathode, LED4.cathode, Part1.A0, Part1.GND
  N2: LED1.anode, R4.Pin_0
  N3: LED2.anode, R3.Pin_0
  N4: LED3.anode, R2.Pin_0
  N5: LED4.anode, R1.Pin_1
  N6: R1.Pin_0, Part1.D0/RX
  N7: R2.Pin_1, Part1.D1/TX
  N8: R3.Pin_1, Part1.D2
  N9: R4.Pin_1, Part1.D3_PWM
